// Logisim project project_2.circ as structural Verilog: 2 circuits, main circuit main
module main (
);

  wire and_1_out, button_1_out, j_k_ff_1_q, j_k_ff_1_qn, j_k_ff_2_q, j_k_ff_2_qn, j_k_ff_3_q, j_k_ff_3_qn,
       j_k_ff_4_q, n4_bit_decoder_7_display_1_seg1, n4_bit_decoder_7_display_1_seg2,
       n4_bit_decoder_7_display_1_seg3, n4_bit_decoder_7_display_1_seg4, n4_bit_decoder_7_display_1_seg5,
       n4_bit_decoder_7_display_1_seg6, n4_bit_decoder_7_display_1_seg7;

  Button button_1 (.out(button_1_out));
  J_K_Flip_Flop j_k_ff_1 (
    .J(1'b1), .clk(button_1_out), .K(1'b1), .Q(j_k_ff_1_q), .Qn(j_k_ff_1_qn), .reset(and_1_out));  // open: preset, en
  // NOT_Gate not_1 has open pins: in=j_k_ff_1_q, out=open
  J_K_Flip_Flop j_k_ff_2 (
    .J(1'b1), .clk(j_k_ff_1_qn), .K(1'b1), .Q(j_k_ff_2_q), .Qn(j_k_ff_2_qn), .reset(and_1_out));  // open: preset, en
  // NOT_Gate not_2 has open pins: in=j_k_ff_2_q, out=open
  J_K_Flip_Flop j_k_ff_3 (
    .J(1'b1), .clk(j_k_ff_2_qn), .K(1'b1), .Q(j_k_ff_3_q), .Qn(j_k_ff_3_qn), .reset(and_1_out));  // open: preset, en
  // NOT_Gate not_3 has open pins: in=j_k_ff_3_q, out=open
  J_K_Flip_Flop j_k_ff_4 (
    .J(1'b1), .clk(j_k_ff_3_qn), .K(1'b1), .Q(j_k_ff_4_q), .reset(and_1_out));  // open: Qn, preset, en
  // NOT_Gate not_4 has open pins: in=j_k_ff_4_q, out=open
  _4_bit_decoder__7_display u_4_bit_decoder_7_display_1 (
    .A(j_k_ff_4_q), .B(j_k_ff_3_q), .C(j_k_ff_2_q), .D(j_k_ff_1_q), .Seg1(n4_bit_decoder_7_display_1_seg1),
    .Seg2(n4_bit_decoder_7_display_1_seg2), .Seg3(n4_bit_decoder_7_display_1_seg3),
    .Seg4(n4_bit_decoder_7_display_1_seg4), .Seg5(n4_bit_decoder_7_display_1_seg5),
    .Seg6(n4_bit_decoder_7_display_1_seg6), .Seg7(n4_bit_decoder_7_display_1_seg7));
  and and_1 (and_1_out, j_k_ff_2_q, j_k_ff_4_q);
  _7_Segment_Display u_7_segment_display_1 (
    .g(n4_bit_decoder_7_display_1_seg4), .f(n4_bit_decoder_7_display_1_seg3),
    .a(n4_bit_decoder_7_display_1_seg2), .b(n4_bit_decoder_7_display_1_seg1),
    .e(n4_bit_decoder_7_display_1_seg7), .d(n4_bit_decoder_7_display_1_seg6),
    .c(n4_bit_decoder_7_display_1_seg5));  // open: dp
endmodule

module _4_bit_decoder__7_display (
  input  A,
  input  B,
  input  C,
  input  D,
  output Seg1,
  output Seg2,
  output Seg3,
  output Seg4,
  output Seg5,
  output Seg6,
  output Seg7
);

  wire and_1_out, and_2_out, and_3_out, and_4_out, and_5_out, and_6_out, and_7_out, and_8_out, and_9_out,
       and_10_out, and_11_out, and_12_out, and_13_out, and_14_out, and_15_out, and_16_out, and_17_out,
       and_18_out, and_19_out, and_20_out, and_21_out, and_22_out, and_23_out, and_24_out, and_25_out,
       not_1_out, not_2_out, not_3_out, not_4_out, not_5_out, not_6_out, not_7_out, not_8_out, not_9_out,
       not_10_out, not_11_out, not_12_out, not_13_out, not_14_out, not_15_out, not_16_out, not_17_out,
       not_18_out, not_19_out, not_20_out, not_21_out, not_22_out, not_23_out, not_24_out, not_25_out,
       not_26_out, not_27_out, not_28_out, not_29_out, not_30_out, not_31_out, not_32_out, not_33_out,
       not_34_out, not_35_out, not_36_out, not_37_out, not_38_out, not_39_out, not_40_out, not_41_out,
       not_42_out, not_43_out, not_44_out, not_45_out, not_46_out, not_47_out, not_48_out, not_49_out,
       not_50_out, not_51_out;

  not not_1 (not_1_out, A);
  and and_1 (and_1_out, not_1_out, not_2_out);
  not not_2 (not_2_out, B);
  not not_3 (not_3_out, A);
  and and_2 (and_2_out, not_3_out, not_4_out, not_5_out);
  not not_4 (not_4_out, C);
  not not_5 (not_5_out, D);
  not not_6 (not_6_out, B);
  and and_3 (and_3_out, not_6_out, not_7_out);
  not not_7 (not_7_out, C);
  not not_8 (not_8_out, A);
  and and_4 (and_4_out, not_8_out, C, D);
  and and_5 (and_5_out, A, not_9_out, not_10_out);
  not not_9 (not_9_out, B);
  not not_10 (not_10_out, C);
  not not_11 (not_11_out, A);
  and and_6 (and_6_out, not_11_out, B, D);
  not not_12 (not_12_out, A);
  not not_13 (not_13_out, B);
  and and_7 (and_7_out, not_12_out, not_13_out, C);
  not not_14 (not_14_out, A);
  and and_8 (and_8_out, not_14_out, not_15_out, not_16_out);
  not not_15 (not_15_out, B);
  not not_16 (not_16_out, D);
  and and_9 (and_9_out, A, not_17_out, not_18_out);
  not not_17 (not_17_out, B);
  not not_18 (not_18_out, C);
  not not_19 (not_19_out, A);
  and and_10 (and_10_out, not_19_out, B, not_20_out);
  not not_20 (not_20_out, C);
  not not_21 (not_21_out, A);
  and and_11 (and_11_out, not_21_out, not_22_out, not_23_out);
  not not_22 (not_22_out, C);
  not not_23 (not_23_out, D);
  not not_24 (not_24_out, A);
  and and_12 (and_12_out, not_24_out, B, not_25_out);
  not not_25 (not_25_out, D);
  not not_26 (not_26_out, B);
  and and_13 (and_13_out, A, not_26_out, not_27_out);
  not not_27 (not_27_out, C);
  not not_28 (not_28_out, A);
  and and_14 (and_14_out, not_28_out, B, not_29_out);
  not not_29 (not_29_out, C);
  not not_30 (not_30_out, A);
  not not_31 (not_31_out, B);
  and and_15 (and_15_out, not_30_out, not_31_out, C);
  not not_32 (not_32_out, A);
  and and_16 (and_16_out, not_32_out, C, not_33_out);
  not not_33 (not_33_out, D);
  not not_34 (not_34_out, B);
  and and_17 (and_17_out, not_34_out, not_35_out);
  not not_35 (not_35_out, C);
  not not_36 (not_36_out, A);
  and and_18 (and_18_out, not_36_out, D);
  not not_37 (not_37_out, A);
  and and_19 (and_19_out, not_37_out, B);
  not not_38 (not_38_out, B);
  not not_39 (not_39_out, C);
  not not_40 (not_40_out, D);
  not not_41 (not_41_out, A);
  not not_42 (not_42_out, C);
  not not_43 (not_43_out, A);
  not not_44 (not_44_out, B);
  not not_45 (not_45_out, A);
  not not_46 (not_46_out, D);
  not not_47 (not_47_out, B);
  not not_48 (not_48_out, C);
  and and_20 (and_20_out, not_47_out, not_48_out, not_49_out);
  not not_49 (not_49_out, D);
  not not_50 (not_50_out, A);
  and and_21 (and_21_out, not_50_out, C, not_51_out);
  not not_51 (not_51_out, D);
  or or_1 (Seg1, and_1_out, and_2_out, and_3_out, and_4_out);
  or or_2 (Seg2, and_5_out, and_6_out, and_7_out, and_8_out);
  or or_3 (Seg3, and_9_out, and_10_out, and_11_out, and_12_out);
  or or_4 (Seg4, and_13_out, and_14_out, and_15_out, and_16_out);
  or or_5 (Seg5, and_17_out, and_18_out, and_19_out);
  and and_22 (and_22_out, not_38_out, not_39_out, not_40_out);
  and and_23 (and_23_out, not_41_out, B, not_42_out, D);
  and and_24 (and_24_out, not_43_out, not_44_out, C);
  and and_25 (and_25_out, not_45_out, C, not_46_out);
  or or_6 (Seg7, and_20_out, and_21_out);
  or or_7 (Seg6, and_22_out, and_23_out, and_24_out, and_25_out);
endmodule
